# Fritzing sketch xcsoar_remote (saved by Fritzing 0.9.6b)

parts:
  Bauteil1 = Arduino Pro Micro (Clone)
  S1 = Momentary Switch [package=ksa_sealed_tac_switch]
  S2 = Momentary Switch [package=ksa_sealed_tac_switch]
  S3 = Momentary Switch [package=ksa_sealed_tac_switch]
  S4 = Momentary Switch [package=ksa_sealed_tac_switch]

nets:
  N1: Bauteil1.GND, S1.2, S2.2, S3.2, S4.2
  N2: Bauteil1.D6, S1.4
  N3: Bauteil1.D7, S3.4
  N4: Bauteil1.D8, S4.4
  N5: Bauteil1.D9, S2.4
